# Fritzing sketch 5 12V Relais (saved by Fritzing 0.9.2b)
breadboards: 1

parts:
  Arduino_MEGA_2560 = Arduino Mega 2560 (Rev3)
  12V_Power = Power plug
  Q2 = Basic FET P-Channel [package="TO220 [THT]"]
  Q3 = Basic FET P-Channel [package="TO220 [THT]"]
  Q4 = Basic FET P-Channel [package="TO220 [THT]"]
  Q1 = Basic FET P-Channel [package="TO220 [THT]"]
  R5 = Resistor [tolerance=±5% resistance=220 package=THT]
  R4 = Resistor [tolerance=±5% resistance=220 package=THT]
  R3 = Resistor [tolerance=±5% resistance=220 package=THT]
  R2 = Resistor [tolerance=±5% resistance=220 package=THT]
  R1 = Resistor [tolerance=±5% resistance=220 package=THT]
  Q5 = Basic FET P-Channel [package="TO220 [THT]"]
  M2 = DC Motor
  M3 = DC Motor
  M4 = DC Motor
  M5 = DC Motor
  M1 = DC Motor
  D1 = Rectifier Diode [part_number=1N4001 package="300 mil [THT]"]  # not connected
  D2 = Rectifier Diode [part_number=1N4001 package="300 mil [THT]"]  # not connected
  D3 = Rectifier Diode [part_number=1N4001 package="300 mil [THT]"]  # not connected
  D4 = Rectifier Diode [part_number=1N4001 package="300 mil [THT]"]  # not connected
  D5 = Rectifier Diode [part_number=1N4001 package="300 mil [THT]"]  # not connected

nets:
  N1: Arduino_MEGA_2560.D0_RX0, R5.Pin_0
  N2: Arduino_MEGA_2560.D1_TX0, R4.Pin_0
  N3: Arduino_MEGA_2560.D2_PWM, R3.Pin_0
  N4: Arduino_MEGA_2560.D3_PWM, R2.Pin_0
  N5: Arduino_MEGA_2560.D4_PWM, R1.Pin_0
  N6: 12V_Power.GND, M2.pin_1, M3.pin_1, M4.pin_1, M5.pin_1, M1.pin_1
  N7: 12V_Power.VCC, Q2.gate, Q3.gate, Q4.gate, Q1.gate, Q5.gate
  N8: Q2.source, M2.pin_2
  N9: Q3.source, M3.pin_2
  N10: Q4.source, M4.pin_2
  N11: Q1.source, M1.pin_2
  N12: Q5.source, M5.pin_2
